# Fritzing sketch arduino (saved by Fritzing 0.9.3b)

parts:
  Часть1 = Arduino Uno (Rev3) - ICSP
  hc-sr1 = hc-sr04

nets:
  N1: Часть1.D9_PWM, hc-sr1.Echo
  N2: Часть1.D10_PWM/SS, hc-sr1.Trig
  5V: Часть1.5V, hc-sr1.VCC
  GND: Часть1.GND, hc-sr1.GND
