# Fritzing sketch running_man (saved by Fritzing 0.9.3b)
breadboards: 1

parts:
  Часть1 = Arduino Uno (Rev3)
  J1 = Piezo Speaker
  R1 = Resistor [tolerance=±5% resistance=220 package=THT]
  R2 = Resistor [tolerance=±5% resistance=220 package=THT]
  R3 = Resistor [tolerance=±5% resistance=220 package=THT]
  R4 = Resistor [tolerance=±5% resistance=220 package=THT]
  LED1 = LED - 5mm [color="Orange (605nm)" package="5 mm [THT]"]
  LED2 = LED - 5mm [color="Red (633nm)" package="5 mm [THT]"]
  LED3 = LED - 5mm [color="Green (555nm)" package="5 mm [THT]"]
  S1 = Momentary Switch [package=ksa_sealed_tac_switch]

nets:
  N1: Часть1.D8, R1.Pin_0
  N2: Часть1.D10_PWM/SS, R2.Pin_0
  N3: Часть1.D11_PWM/MOSI, R3.Pin_0
  N4: Часть1.D12/MISO, R4.Pin_0
  N5: Часть1.D3_PWM, S1.1
  N6: Часть1.5V, S1.3
  N7: Часть1.GND, J1.pin1, LED1.cathode, LED2.cathode, LED3.cathode
  N8: J1.pin2, R1.Pin_1
  N9: R2.Pin_1, LED3.anode
  N10: R3.Pin_1, LED1.anode
  N11: R4.Pin_1, LED2.anode
